# Fritzing sketch Plano (saved by Fritzing 0.9.3b)
breadboards: 1

parts:
  Componente1 = Arduino Uno (Rev3)
  LED1 = LED - 5mm [color="Green (560nm)" package="5 mm [THT]"]  # not connected
  LED2 = LED - 5mm [color="Red (633nm)" package="5 mm [THT]"]  # not connected
  LED3 = LED - 5mm [color="Yellow (595nm)" package="5 mm [THT]"]  # not connected
  LED4 = LED - 5mm [color="Red (633nm)" package="5 mm [THT]"]  # not connected
  LED5 = LED - 5mm [color="Green (560nm)" package="5 mm [THT]"]  # not connected
  hc-sr1 = hc-sr04
  R1 = Resistor [tolerance=±5% resistance=220 package="0805 [SMD]"]  # not connected
  J1 = Piezo Speaker  # not connected
  S1 = Pushbutton [package="[THT]"]
  R2 = Resistor [tolerance=±5% resistance=220 package="0805 [SMD]"]
  R3 = Resistor [tolerance=±5% resistance=220 package="0805 [SMD]"]
  R4 = Resistor [tolerance=±5% resistance=220 package="0805 [SMD]"]
  R5 = Resistor [tolerance=±5% resistance=220 package="0805 [SMD]"]
  R6 = Resistor [tolerance=±5% resistance=10k package="0805 [SMD]"]

nets:
  N1: Componente1.D8, S1.Pin_3, R6.Pin_1
  N2: Componente1.D9_PWM, hc-sr1.Echo
  N3: Componente1.D10_PWM/SS, hc-sr1.Trig
  5V: Componente1.5V, hc-sr1.VCC, S1.Pin_1
  GND: Componente1.GND, hc-sr1.GND, R2.Pin_0, R3.Pin_0, R4.Pin_0, R5.Pin_0
